# Fritzing sketch isp (saved by Fritzing 0.9.3b)
breadboards: 1

parts:
  Raspberry_Pi_1 = Raspberry Pi 3 [part_number=RPI-3-V1.2]
  J1 = female pin header, 2 pins [form="♀ (female)"]
  J2 = female pin header, 2 pins [form="♀ (female)"]
  J3 = female pin header, 2 pins [form="♀ (female)"]
  R2 = Resistor [tolerance=±5% resistance=1.5k package=THT]
  R1 = Resistor [tolerance=±5% resistance=2.7k package=THT]

nets (from the breadboard view):
  N1: Raspberry_Pi_1.GPIO3, Raspberry_Pi_1.GND, J1.pin1, R1.Pin_1
  N2: Raspberry_Pi_1.GIPO10, J2.pin1
  N3: Raspberry_Pi_1.GIPO9, R2.Pin_1, R1.Pin_0
  N4: Raspberry_Pi_1.GIPO11, J2.pin2
  N5: Raspberry_Pi_1.GIPO14, J1.pin2
  N6: J3.pin2, R2.Pin_0

notes:
  5 3 1
  6 4 2
